# Fritzing sketch ShyBox (saved by Fritzing 0.9.3b)
breadboards: 1

parts:
  DFPlayer_Mini1 = DFPlayer MINI [package="DIP (Dual Inline) [THT]"]
  hc-sr1 = hc-sr04
  Linh_kiện1 = Arduino Uno (Rev3) - ICSP
  SP1 = SPEAKER [package=pcb_mount_speaker]
  SW-1 = Vibration sensor module
  J1 = Basic Servo
  J2 = Basic Servo
  J3 = Basic Servo

nets:
  VCC: DFPlayer_Mini1.VCC, hc-sr1.VCC, Linh_kiện1.5V, SW-1.vcc
  N1: DFPlayer_Mini1.RX, Linh_kiện1.D11_PWM/MOSI
  N2: DFPlayer_Mini1.TX, Linh_kiện1.D10_PWM/SS
  N3: DFPlayer_Mini1.SPK1, SP1.-
  GND: DFPlayer_Mini1.GND, hc-sr1.GND, Linh_kiện1.GND, SW-1.Ground, J2.gnd
  N4: DFPlayer_Mini1.SPK2, SP1.+
  N5: hc-sr1.Trig, Linh_kiện1.A1
  N6: hc-sr1.Echo, Linh_kiện1.A2
  N7: Linh_kiện1.D2, J1.pulse
  N8: Linh_kiện1.D3_PWM, J2.pulse
  N9: Linh_kiện1.D4, J3.pulse
  N10: Linh_kiện1.D5_PWM, SW-1.Digital_output
  VIN: Linh_kiện1.VIN, J2.vcc

custom parts:
  DFPlayer MINI: MP3 module by DFRobot.com for playing Music from an SD-Card. Supports WAV and MP3 files.
  Vibration sensor module: Single-roller type full induction trigger switch. When no vibration or tilt, the product is ON conduction state, and in the steady state, when a vibration or tilt, the switch will be rendered instantly disconnect the conductive resistance increases, generating a current pulse signal, thereby triggering circuit. The default state of the swith is close Digital output Supply voltage:3.3V-5V On-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
